# Fritzing sketch traffic_light_breadboard_dgrm (saved by Fritzing 0.9.3b)
breadboards: 1

parts:
  R1 = Resistor [tolerance=±5% resistance=220 package=THT]
  Raspberry_Pi_1 = Raspberry Pi 3 [part_number=RPI-3-V1.2]
  R2 = Resistor [tolerance=±5% resistance=220 package=THT]
  R3 = Resistor [tolerance=±5% resistance=220 package=THT]
  LED1 = LED - 5mm [color="Red (633nm)" package="5 mm [THT]"]
  LED2 = LED - 5mm [color="Yellow (595nm)" package="5 mm [THT]"]
  LED3 = LED - 5mm [color="Green (565nm)" package="5 mm [THT]"]

nets:
  N1: R1.Pin_0, Raspberry_Pi_1.GPIO17
  N2: R1.Pin_1, LED1.anode
  N3: Raspberry_Pi_1.GPIO27, R3.Pin_0
  N4: Raspberry_Pi_1.GPIO18, R2.Pin_0
  N5: Raspberry_Pi_1.GND, LED1.cathode, LED3.cathode
  N6: R2.Pin_1, LED2.anode
  N7: R3.Pin_1, LED3.anode
